# Fritzing sketch LumiMonitor_MotionSensor (saved by Fritzing 0.9.3b)
circuit board: 3.85683cm x 3.40961cm
breadboards: 1

parts:
  PIR_Moition_Sensor = Grove Light Sensor
  Raspberry_Pi_1 = Raspberry Pi 3 [part_number=RPI-3-V1.2]

nets:
  GND: PIR_Moition_Sensor.GND, Raspberry_Pi_1.GND
  VCC: PIR_Moition_Sensor.VCC, Raspberry_Pi_1.5V
  N1: PIR_Moition_Sensor.SIG, Raspberry_Pi_1.GPIO18

notes:
  Kyle Voduris
  N01246531
  D1
  NC
  VCC
  GND
