# Fritzing sketch LumiMonitor_MotionSensor2 (saved by Fritzing 0.9.3b)
circuit board: 2.93431cm x 3.05719cm
breadboards: 1

parts:
  PIR_Moition_Sensor = Grove Light Sensor
  J1 = female pin header, 3 pins [form="♀ (female)"]

nets:
  N1: PIR_Moition_Sensor.GND, J1.pin1
  N2: PIR_Moition_Sensor.VCC, J1.pin2
  N3: PIR_Moition_Sensor.SIG, J1.pin3

notes:
  Kyle Voduris
  N01246531
  D1
  NC
  VCC
  GND
